# Fritzing sketch Project 2019 (saved by Fritzing 0.9.3b)
breadboards: 1

parts:
  Q1 = NPN-Transistor [package="TO92 [THT]"]
  D1 = Rectifier Diode [part_number=1N4001 package="300 mil [THT]"]
  R1 = Resistor [tolerance=±5% resistance=220 package=THT]
  LED1 = RGB LED (com. cathode, rgb) [package="5 mm [THT]"]
  M1 = DC Motor
  Part1 = Arduino Mega ADK (Rev3)
  Part2 = Bluetooth HC-05 Macho
  Part3 = Soil Moisture Sensor

nets:
  N1: Q1.E, R1.Pin_1
  N2: Q1.B, D1.anode, M1.pin_1
  GND: Q1.C, LED1.blue_anode, Part1.GND, Part2.GND, Part3.GND
  VCC: D1.cathode, M1.pin_2, Part1.IOREF, Part1.5V, Part2.VCC, Part3.VCC
  N3: R1.Pin_0, Part1.D2_PWM
  N4: LED1.red_anode, Part1.D10_PWM
  N5: LED1.common_cathode, Part1.D9_PWM
  N6: LED1.green_anode, Part1.D11_PWM
  N7: Part1.A0, Part3.SIG
  N8: Part1.D0/RX0, Part2.TXD
  N9: Part1.D1/TX0, Part2.RXD
